# Fritzing sketch BehaviourStates (saved by Fritzing 0.9.3b)
breadboards: 1

parts:
  R1 = Resistor [tolerance=±5% resistance=1M package=THT]
  Phototransistor1 = LTR-301 [package=ltr-301]
  Arduino = Arduino Nano (Rev3.0)
  R2 = Resistor [tolerance=±5% resistance=220 package=THT]
  LED1 = LED - 5mm [color="Red (633nm)" package="5 mm [THT]"]
  S1 = Momentary Switch [package=ksa_sealed_tac_switch]
  R3 = Resistor [tolerance=±5% resistance=10k package="2010 [SMD]"]
  NPN = NPN-Transistor [package="TO92 [THT]"]
  R4 = Resistor [tolerance=±5% resistance=1k package="2010 [SMD]"]

nets:
  N1: R1.Pin_0, Phototransistor1.E, Arduino.D2
  N2: R1.Pin_1, Arduino.GND, R3.Pin_1, NPN.E
  N3: Phototransistor1.C, Arduino.5V, LED1.anode, S1.4
  N4: Arduino.D3, R4.Pin_1
  N5: Arduino.D4, S1.1
  N6: R2.Pin_0, LED1.cathode
  N7: R2.Pin_1, NPN.C
  N8: S1.2, R3.Pin_0
  N9: NPN.B, R4.Pin_0
