# Fritzing sketch Experimentation (saved by Fritzing 0.9.3b)
breadboards: 1

parts:
  R1 = Resistor [tolerance=±5% resistance=1M package=THT]
  Phototransistor1 = LTR-301 [package=ltr-301]
  Arduino = Arduino Nano (Rev3.0)
  R2 = Resistor [tolerance=±5% resistance=220 package=THT]
  LED1 = LED - 5mm [color="Red (633nm)" package="5 mm [THT]"]

nets:
  N1: R1.Pin_0, Phototransistor1.E, Arduino.D2, Arduino.A0
  N2: R1.Pin_1, Arduino.GND, R2.Pin_1
  N3: Phototransistor1.C, Arduino.5V, LED1.anode
  N4: R2.Pin_0, LED1.cathode
