# Fritzing sketch EdgesDetection (saved by Fritzing 0.9.3b)
breadboards: 1

parts:
  Composant2 = Arduino Nano (Rev3.0)
  R1 = Resistor [tolerance=±5% resistance=1k package=THT]
  Q1 = LTR-301 [package=ltr-301]

nets:
  N1: Composant2.GND, R1.Pin_0
  N2: Composant2.D2, R1.Pin_1, Q1.E
  N3: Composant2.5V, Q1.C
