# Fritzing sketch shutterSpeedTester (saved by Fritzing 0.9.3b)
breadboards: 1

parts:
  Composant2 = Arduino Nano (Rev3.0)
  R1 = Resistor [tolerance=±5% resistance=1k package=THT]
  Q1 = LTR-301 [package=ltr-301]
  LCD1 = LCD screen
  U1 = POT [package=pot_alpha_rv16af-20]

nets:
  GND: Composant2.GND, R1.Pin_0, LCD1.VSS, LCD1.R/W, LCD1.LED-, U1.A
  N1: Composant2.D2, R1.Pin_1, Q1.E
  N2: Composant2.D3, LCD1.DB4
  N3: Composant2.D4, LCD1.DB5
  N4: Composant2.D5, LCD1.DB6
  N5: Composant2.D6, LCD1.DB7
  N6: Composant2.D11/MOSI, LCD1.RS
  N7: Composant2.D12/MISO, LCD1.E
  5V: Composant2.5V, Q1.C, LCD1.VDD, LCD1.LED+, U1.E
  N8: LCD1.V0, U1.S
